# Fritzing sketch Countdown Timer (saved by Fritzing 1.0.5)
circuit board: 8.46667cm x 5.64444cm
breadboards: 1

parts:
  Mod1 = Amica NodeMCU DEVKIT 1.0
  Grove1 = Grove OLED 128x96
  S1 = Pushbutton [package="[THT]"]
  S2 = Pushbutton [package="[THT]"]
  S3 = Pushbutton [package="[THT]"]

nets:
  N1: Mod1.pin1, Mod1.pin_10, Mod1.pin_26, Grove1.VCC
  N2: Mod1.pin2, Mod1.pin_9, Mod1.pin_25, Mod1.pin_29, Grove1.GND, S1.Pin_3, S1.Pin_4, S2.Pin_3, S2.Pin_4, S3.Pin_3, S3.Pin_4
  N3: Mod1.pin_11, S3.Pin_1, S3.Pin_2
  N4: Mod1.pin_12, S1.Pin_1, S1.Pin_2
  N5: Mod1.pin_13, Grove1.SDA
  N6: Mod1.pin_14, Grove1.SCL
  N7: Mod1.pin_19, S2.Pin_1, S2.Pin_2

notes:
  Start
  Decrease
  Increase
