# Fritzing sketch pid_line_follower (saved by Fritzing 1.0.5)
breadboards: 2

parts:
  Part1 = Arduino Uno (Rev3)
  YwRobot_Power_Supply1 = YwRobot Breadboard Power Supply [part_number=545043]
  M1 = gear-motor
  M2 = gear-motor
  M3 = fc-51 [package=THT]
  M4 = fc-51 [package=THT]
  M5 = fc-51 [package=THT]
  M6 = fc-51 [package=THT]
  M7 = fc-51 [package=THT]
  L298N1 = L298N DC motor driver
  C1 = Electrolytic Capacitor [capacitance=470µF voltage=25V package="200 mil [THT, electrolytic]"]
  C2 = Electrolytic Capacitor [capacitance=470µF voltage=25V package="200 mil [THT, electrolytic]"]
  C4 = Electrolytic Capacitor [capacitance=1μF voltage=50V package="0405 [SMD, electrolytic]"]
  C6 = Ceramic Capacitor [capacitance=104pF voltage=35V package="0805 [SMD, multilayer]"]

nets:
  N1: Part1.A0, M7.pin1
  N2: Part1.A1, M3.pin1
  N3: Part1.A2, M6.pin1
  N4: Part1.A3, M4.pin1
  N5: Part1.A4/SDA, M5.pin1
  N6: Part1.D8, L298N1.IN1
  N7: Part1.D9_PWM, L298N1.IN2
  N8: Part1.D12/MISO, L298N1.IN3
  N9: Part1.D13/SCK, L298N1.IN4
  GND: Part1.GND, YwRobot_Power_Supply1.GND#13, YwRobot_Power_Supply1.GND#14, M3.pin2, M4.pin2, M5.pin2, M6.pin2, M7.pin2, L298N1.GND, C1.-, C2.-, C4.-, C6.0
  N10: Part1.D5_PWM, L298N1.ENA
  N11: Part1.D6_PWM, L298N1.ENB
  5V: Part1.5V, M3.pin3, M4.pin3, M5.pin3, M6.pin3, M7.pin3, L298N1.5V
  N12: YwRobot_Power_Supply1.VCC#5, YwRobot_Power_Supply1.VCC#6
  N13: YwRobot_Power_Supply1.VCC#9, YwRobot_Power_Supply1.VCC#10, L298N1.12V, C1.+, C2.+, C4.+, C6.1
  N14: YwRobot_Power_Supply1.GND#11, YwRobot_Power_Supply1.GND#12
  N15: M1.pin_1, L298N1.OUT4
  N16: M1.pin_2, L298N1.OUT3
  N17: M2.pin_1, L298N1.OUT2
  N18: M2.pin_2, L298N1.OUT1

custom parts:
  YwRobot Breadboard Power Supply: The YwRobot Breadboard Power Supply (MB-V2) has two power rails; they can be 5V or 3V3. Power to the module can be provided through the female USB socket or through the A10 (female) 2.1mm power jack.
  L298N DC motor driver: 2x DC motor driver with 78M05 positive voltage regulator (7..35 V) L298N: max 46 V, 2 A Set 5 V Enable jumper to enable 5 V regultor (needed for the L298N) and +5 V output at screw terminal or supply external +5 V at screw terminal Set ENA and/or ENB to +5 V to enable motor permanently or supply ENA and/or ENB with PWM signal IN1 and IN2 set rotation directory for motor A (OUT1/OUT2) IN2 and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
