# Fritzing sketch Wifi controlled robot (saved by Fritzing 1.0.5)
breadboards: 1

parts:
  YwRobot_Power_Supply1 = YwRobot Breadboard Power Supply [part_number=545043]
  Mod1 = Amica NodeMCU DEVKIT 1.0
  L298N1 = L298N DC motor driver
  M1 = gear-motor
  M2 = gear-motor

nets:
  N1: YwRobot_Power_Supply1.VCC#5, YwRobot_Power_Supply1.VCC#6
  N2: YwRobot_Power_Supply1.VCC#9, YwRobot_Power_Supply1.VCC#10, L298N1.12V
  N3: YwRobot_Power_Supply1.GND#11, YwRobot_Power_Supply1.GND#12
  N4: YwRobot_Power_Supply1.GND#13, YwRobot_Power_Supply1.GND#14, Mod1.pin2, Mod1.pin_9, Mod1.pin_25, Mod1.pin_29, L298N1.GND
  N5: Mod1.pin1, Mod1.pin_10, Mod1.pin_26, L298N1.5V
  N6: Mod1.pin6, L298N1.ENB
  N7: Mod1.pin7, L298N1.IN4
  N8: Mod1.pin8, L298N1.IN3
  N9: Mod1.pin_12, L298N1.ENA
  N10: Mod1.pin_14, L298N1.IN2
  N11: Mod1.pin_15, L298N1.IN1
  N12: L298N1.OUT1, M2.pin_2
  N13: L298N1.OUT2, M2.pin_1
  N14: L298N1.OUT3, M1.pin_2
  N15: L298N1.OUT4, M1.pin_1

custom parts:
  YwRobot Breadboard Power Supply: The YwRobot Breadboard Power Supply (MB-V2) has two power rails; they can be 5V or 3V3. Power to the module can be provided through the female USB socket or through the A10 (female) 2.1mm power jack.
  L298N DC motor driver: 2x DC motor driver with 78M05 positive voltage regulator (7..35 V) L298N: max 46 V, 2 A Set 5 V Enable jumper to enable 5 V regultor (needed for the L298N) and +5 V output at screw terminal or supply external +5 V at screw terminal Set ENA and/or ENB to +5 V to enable motor permanently or supply ENA and/or ENB with PWM signal IN1 and IN2 set rotation directory for motor A (OUT1/OUT2) IN2 and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
